# Fritzing sketch Sketch_Steckplatine (saved by Fritzing 0.9.3b)
breadboards: 1

parts:
  U1 = ESP8266 WiFi Module [part_number=ESP8266]
  R1 = Resistor [tolerance=±5% resistance=10k package="2512 [SMD]"]
  R2 = Resistor [tolerance=±5% resistance=10k package="2512 [SMD]"]
  R3 = Resistor [tolerance=±5% resistance=10k package="2512 [SMD]"]
  R4 = Resistor [tolerance=±5% resistance=10k package="2512 [SMD]"]
  Bauteil1 = FTDI Basic Programmer
  R5 = Resistor [tolerance=±5% resistance=1.2k package="2512 [SMD]"]
  S2 = Toggle Switch [package=THT]
  S1 = Toggle Switch [package=THT]

nets:
  N1: U1.RXD_GPIO_3, S2.COM
  N2: U1.VCC, R1.Pin_0, R2.Pin_0
  N3: U1.GPIO_0, S1.COM
  N4: U1.EXT_RST, R1.Pin_1
  N5: U1.GPIO_2, R4.Pin_1, R5.Pin_0
  N6: U1.CH_PD, R2.Pin_1
  GND: U1.GND, R3.Pin_0, Bauteil1.GND
  N7: U1.TXD_GPIO_1, Bauteil1.RXI
  N8: R3.Pin_1, S1.L2
  N9: R4.Pin_0, S1.L1
  N10: Bauteil1.TXO, S2.L2

notes:
  Connects to garage open sensor; high when closed, otherwise floating; this ensures that on startup GPIO_2 is high or floating, which is necessary for boot
  Connects to optocoupler, which switches the relay that toggles the state of the garage door
  The two switches toggle the state of the chip on startup; when they are both left, it starts normally and is able to control the garage door. Are both right, it enters programming mode on startup (as CH_PD is low) and is able to be programmed by the FTDI (as RX GPIO_3 is now used as RX instead of an output).
  For startup of the Chip (regardless of mode), CH_PD and EXT_RST must be high and GPIO_2 must be floating or high. As we want to use GPIO_2 for reading the status of the garage door sensor (in normal mode), we need to ensure that after bootup he is pulled low, such that he properly reads the open state of the garage door as low. Therefore, we pull GPIO_0 low after startup. Because the resistor between GPIO_0 and GPIO_2 has 10kΩ and the resistor to the garage sensor only has 1.2Ω, the state will still be read properly.
  This doesn't cause problems for normal mode startup, which requires GPIO_0 to be high, as GPIO_2 always tries to pull high on startup, setting GPIO_0 high by default.

custom parts:
  ESP8266 WiFi Module: Generic WiFi Module based on the ESP8266 with onboard PCB antenna and UART communications
